// Logisim project 4-1mux与非门.circ as structural Verilog
module _4_1MUX (
  input  D0,
  input  D1,
  input  D2,
  input  D3,
  input  S0,
  input  S1,
  output Y
);

  wire nand_1_out, nand_2_out, nand_3_out, nand_4_out, nand_5_out, nand_6_out, nand_7_out, nand_8_out;

  nand nand_1 (nand_1_out, S0, S0);
  nand nand_2 (nand_2_out, S1, S1);
  nand nand_3 (nand_3_out, S0, S0);
  nand nand_4 (nand_4_out, S1, S1);
  nand nand_5 (nand_5_out, D3, S0, S1);
  nand nand_6 (nand_6_out, D2, nand_1_out, S1);
  nand nand_7 (nand_7_out, D1, S0, nand_2_out);
  nand nand_8 (nand_8_out, D0, nand_3_out, nand_4_out);
  nand nand_9 (Y, nand_5_out, nand_6_out, nand_7_out, nand_8_out);
endmodule
