// Logisim project 4位奇偶校验.circ as structural Verilog: 1 circuit, main circuit main
module main (
  input  D3,
  input  D2,
  input  D1,
  input  D0,
  output Y
);

  wire AND1_out, AND2_out, not_1_out, not_2_out, XOR1_out, XOR2_out;

  xor XOR1 (XOR1_out, D3, D2);
  xor XOR2 (XOR2_out, D1, D0);
  not not_1 (not_1_out, XOR1_out);
  not not_2 (not_2_out, XOR2_out);
  and AND1 (AND1_out, XOR1_out, not_2_out);
  and AND2 (AND2_out, XOR2_out, not_1_out);
  or OR (Y, AND1_out, AND2_out);
endmodule
