// Logisim project lab2.5.circ as structural Verilog: 1 circuit, main circuit main
module main (
  input  [7:0] DataIn,
  input  [2:0] shamt,
  input  L_R,
  input  A_L,
  output [7:0] DataOut
);

  wire [5:4] multiplexer_1_out_2;
  wire [7:0] multiplexer_2_out, multiplexer_3_out, multiplexer_4_out, multiplexer_5_out;
  wire [7:2] multiplexer_1_out;
  wire [7:4] multiplexer_4_out_2;

  Multiplexer #(.width(8), .enable("false")) multiplexer_1 (
    .in0(DataIn), .in1(multiplexer_2_out), .out({multiplexer_1_out_2, multiplexer_1_out}), .sel(shamt[0]));
  Multiplexer #(.select(2), .width(8), .enable("false")) multiplexer_2 (
    .in0({1'b0, DataIn[7:1]}), .in1({{2{DataIn[7]}}, DataIn[6:1]}), .in2({DataIn[6:0], 1'b0}),
    .in3({DataIn[6:0], DataIn[7]}), .out(multiplexer_2_out), .sel({L_R, A_L}));
  Multiplexer #(.select(2), .width(8), .enable("false")) multiplexer_3 (
    .in0({2'b00, multiplexer_1_out_2, multiplexer_1_out[7:4]}),
    .in1({{3{multiplexer_1_out_2[5]}}, multiplexer_1_out_2[4], multiplexer_1_out[7:4]}),
    .in2({multiplexer_1_out, 2'b00}), .in3({multiplexer_1_out, multiplexer_1_out_2}),
    .out(multiplexer_3_out), .sel({L_R, A_L}));
  Multiplexer #(.width(8), .enable("false")) multiplexer_4 (
    .in0({multiplexer_1_out_2, multiplexer_1_out}), .in1(multiplexer_3_out),
    .out({multiplexer_4_out[7], multiplexer_4_out[2:0], multiplexer_4_out_2}), .sel(shamt[1]));
  Multiplexer #(.select(2), .width(8), .enable("false")) multiplexer_5 (
    .in0({4'b0000, multiplexer_4_out[7], multiplexer_4_out[2:0]}),
    .in1({{5{multiplexer_4_out[7]}}, multiplexer_4_out[2:0]}), .in2({multiplexer_4_out_2, 4'b0000}),
    .in3({multiplexer_4_out_2, multiplexer_4_out[7], multiplexer_4_out[2:0]}), .out(multiplexer_5_out),
    .sel({L_R, A_L}));
  Multiplexer #(.width(8), .enable("false")) multiplexer_6 (
    .in0({multiplexer_4_out[7], multiplexer_4_out[2:0], multiplexer_4_out_2}), .in1(multiplexer_5_out),
    .out(DataOut), .sel(shamt[2]));

  // Other names for the same wires on the sheet: Din[7:0] = DataIn; Arth_Logic = A_L; Left_Right = L_R;
  //   Dout[7:0] = DataOut

  // Notes on the sheet:
  //   算术右移1
  //   逻辑左移1
  //   逻辑右移1
  //   循环左移1
  //   逻辑右移2
  //   逻辑左移2
  //   循环左移2
  //   算术右移2
  //   L/R,A/L: 00逻辑右移，01算术右移，10逻辑左移，11：循环左移
  //   输入引脚
  //   请勿修改引脚名称、电路名称及电路封装外观
  //   提示：使用多路选择器级联实现8位桶形移位器，禁止直接使用移位器组件。
  //   逻辑右移4
  //   逻辑左移4
  //   循环左移4
  //   算术右移4
  //   输出引脚
endmodule
