// Logisim project lab3.5.circ as structural Verilog: 1 circuit, main circuit main
module main (
  input  CLK,
  input  LD,
  input  [3:0] HH1,
  input  [3:0] HH0,
  input  [3:0] MM1,
  input  [3:0] MM0,
  input  [3:0] SS1,
  input  [3:0] SS0,
  input  [23:0] in_9,
  output [3:0] HH_H,
  output [3:0] HH_L,
  output [3:0] MM_H,
  output [3:0] MM_L,
  output [3:0] SS_H,
  output [3:0] SS_L,
  output LED_R,
  output LED_G,
  output LED_B,
  output INErr
);

  wire and_1_out, and_2_out, and_3_out, and_4_out, and_5_out, and_6_out, and_7_out, and_8_out, and_9_out,
       and_10_out, and_11_out, and_13_out, and_15_out, and_16_out, and_17_out, cntr4u_4_q0, cntr4u_4_q1,
       cntr4u_4_q3, comparator_1_eq, comparator_1_gt, comparator_2_eq, comparator_3_eq, comparator_3_gt,
       comparator_4_eq, comparator_4_gt, comparator_5_eq, comparator_5_gt, comparator_6_eq, comparator_6_gt,
       comparator_7_eq, comparator_7_gt, comparator_8_eq, comparator_8_gt, comparator_9_eq, comparator_10_eq,
       comparator_11_eq, comparator_12_eq, comparator_13_eq, comparator_14_eq, d_ff_1_q, LED_EN, not_1_out,
       not_2_out, or_1_out, or_2_out, or_3_out, or_4_out, or_5_out, or_6_out, or_7_out, or_8_out, or_9_out;

  and and_1 (and_1_out, LD, not_1_out);
  not not_1 (not_1_out, INErr);
  or or_1 (or_1_out, and_2_out, and_11_out);
  Comparator #(.width(4), .mode("unsigned")) comparator_1 (
    .a(HH1), .b(4'b0011), .gt(comparator_1_gt), .eq(comparator_1_eq));  // open: lt
  Comparator #(.width(4), .mode("unsigned")) comparator_2 (.a(HH1), .b(4'b0010), .eq(comparator_2_eq));  // open: gt, lt
  Comparator #(.width(4), .mode("unsigned")) comparator_3 (
    .a(HH0), .b(4'b0100), .gt(comparator_3_gt), .eq(comparator_3_eq));  // open: lt
  Comparator #(.width(4), .mode("unsigned")) comparator_4 (
    .a(HH0), .b(4'b1010), .gt(comparator_4_gt), .eq(comparator_4_eq));  // open: lt
  Comparator #(.width(4), .mode("unsigned")) comparator_5 (
    .a(MM1), .b(4'b0110), .gt(comparator_5_gt), .eq(comparator_5_eq));  // open: lt
  Comparator #(.width(4), .mode("unsigned")) comparator_6 (
    .a(MM0), .b(4'b1010), .gt(comparator_6_gt), .eq(comparator_6_eq));  // open: lt
  Comparator #(.width(4), .mode("unsigned")) comparator_7 (
    .a(SS1), .b(4'b0110), .gt(comparator_7_gt), .eq(comparator_7_eq));  // open: lt
  Comparator #(.width(4), .mode("unsigned")) comparator_8 (
    .a(SS0), .b(4'b1010), .gt(comparator_8_gt), .eq(comparator_8_eq));  // open: lt
  or or_2 (or_2_out, comparator_1_gt, comparator_1_eq);
  or or_3 (or_3_out, comparator_3_gt, comparator_3_eq);
  or or_4 (or_4_out, comparator_4_gt, comparator_4_eq);
  or or_5 (or_5_out, comparator_5_gt, comparator_5_eq);
  or or_6 (or_6_out, comparator_6_gt, comparator_6_eq);
  or or_7 (or_7_out, comparator_7_gt, comparator_7_eq);
  or or_8 (or_8_out, comparator_8_gt, comparator_8_eq);
  D_Flip_Flop #(.trigger("high"), .enable("true")) d_ff_1 (
    .clk(CLK), .D(LED_EN), .Q(d_ff_1_q), .en(LED_EN), .reset(and_8_out));  // open: Qn, preset
  Hex_Digit_Display hex_digit_display_1 (.value(HH_H));  // open: dp
  CNTR4U cntr4u_1 (
    .CLK(CLK), .LD(and_1_out), .CLR(or_1_out), .Q0(HH_L[0]), .Q1(HH_L[1]), .D0(HH0[0]), .D1(HH0[1]),
    .D2(HH0[2]), .Q2(HH_L[2]), .Q3(HH_L[3]), .D3(HH0[3]), .ENP(LED_EN), .ENT(LED_EN));  // open: RCO
  and and_2 (and_2_out, and_4_out, LED_EN);
  CNTR4U cntr4u_2 (
    .CLK(CLK), .LD(and_1_out), .CLR(and_6_out), .Q0(MM_L[0]), .Q1(MM_L[1]), .D0(MM0[0]), .D1(MM0[1]),
    .D2(MM0[2]), .Q2(MM_L[2]), .Q3(MM_L[3]), .D3(MM0[3]), .ENP(and_13_out), .ENT(and_13_out));  // open: RCO
  CNTR4U cntr4u_3 (
    .CLK(CLK), .LD(and_1_out), .CLR(and_7_out), .Q0(SS_L[0]), .Q1(SS_L[1]), .D0(SS0[0]), .D1(SS0[1]),
    .D2(SS0[2]), .Q2(SS_L[2]), .Q3(SS_L[3]), .D3(SS0[3]), .ENP(1'b1), .ENT(1'b1));  // open: RCO
  and and_3 (and_3_out, comparator_2_eq, or_3_out);
  not not_2 (not_2_out, 1'b0);
  Hex_Digit_Display hex_digit_display_2 (.value(MM_H));  // open: dp
  Hex_Digit_Display hex_digit_display_3 (.value(HH_L), .dp(1'b1));
  and and_4 (and_4_out, HH_L[3], HH_L[0]);
  and and_5 (and_5_out, MM_L[3], MM_L[0]);
  and and_6 (and_6_out, and_13_out, and_5_out);
  and and_7 (and_7_out, SS_L[3], SS_L[0]);
  CNTR4U cntr4u_4 (
    .CLK(CLK), .LD(LED_EN), .CLR(and_8_out), .Q0(cntr4u_4_q0), .Q1(cntr4u_4_q1), .D0(not_2_out), .D1(1'b0),
    .D2(1'b0), .Q2(LED_B), .Q3(cntr4u_4_q3), .D3(1'b0), .ENP(d_ff_1_q), .ENT(d_ff_1_q));  // open: RCO
  and and_8 (and_8_out, cntr4u_4_q3, cntr4u_4_q1);
  Hex_Digit_Display hex_digit_display_4 (.value(SS_H));  // open: dp
  Hex_Digit_Display hex_digit_display_5 (.value(MM_L), .dp(1'b1));
  and and_9 (and_9_out, HH_L[0], HH_L[1]);
  and and_10 (and_10_out, and_5_out, and_15_out);
  or or_9 (or_9_out, or_2_out, and_3_out, or_4_out, or_5_out, or_6_out, or_7_out, or_8_out);
  Hex_Digit_Display hex_digit_display_6 (.value(SS_L), .dp(1'b1));
  and and_11 (and_11_out, and_9_out, HH_H[1], LED_EN);
  and and_12 (LED_EN, and_10_out, and_13_out);
  and and_13 (and_13_out, and_7_out, and_16_out);
  and and_14 (INErr, LD, or_9_out);
  CNTR4U cntr4u_5 (
    .CLK(CLK), .LD(and_1_out), .CLR(and_11_out), .Q0(HH_H[0]), .Q1(HH_H[1]), .D0(HH1[0]), .D1(HH1[1]),
    .D2(HH1[2]), .Q2(HH_H[2]), .Q3(HH_H[3]), .D3(HH1[3]), .ENP(and_2_out), .ENT(and_2_out));  // open: RCO
  CNTR4U cntr4u_6 (
    .CLK(CLK), .LD(and_1_out), .CLR(LED_EN), .Q0(MM_H[0]), .Q1(MM_H[1]), .D0(MM1[0]), .D1(MM1[1]),
    .D2(MM1[2]), .Q2(MM_H[2]), .Q3(MM_H[3]), .D3(MM1[3]), .ENP(and_6_out), .ENT(and_6_out));  // open: RCO
  CNTR4U cntr4u_7 (
    .CLK(CLK), .LD(and_1_out), .CLR(and_13_out), .Q0(SS_H[0]), .Q1(SS_H[1]), .D0(SS1[0]), .D1(SS1[1]),
    .D2(SS1[2]), .Q2(SS_H[2]), .Q3(SS_H[3]), .D3(SS1[3]), .ENP(1'b1), .ENT(and_7_out));  // open: RCO
  xor xor_1 (LED_R, cntr4u_4_q0, cntr4u_4_q1);
  xor xor_2 (LED_G, cntr4u_4_q1, LED_B);
  and and_15 (and_15_out, MM_H[2], MM_H[0]);
  and and_16 (and_16_out, SS_H[2], SS_H[0]);
  // RGBLed RGBLED: pin names not known; wires that end beside it: LED_R, LED_G, LED_B
  Comparator #(.width(4)) comparator_9 (.a(in_9[3:0]), .b(HH_H), .eq(comparator_9_eq));  // open: gt, lt
  Comparator #(.width(4)) comparator_10 (.a(in_9[7:4]), .b(HH_L), .eq(comparator_10_eq));  // open: gt, lt
  Comparator #(.width(4)) comparator_11 (.a(in_9[11:8]), .b(MM_H), .eq(comparator_11_eq));  // open: gt, lt
  Comparator #(.width(4)) comparator_12 (.a(in_9[15:12]), .b(MM_L), .eq(comparator_12_eq));  // open: gt, lt
  Comparator #(.width(4)) comparator_13 (.a(in_9[19:16]), .b(SS_H), .eq(comparator_13_eq));  // open: gt, lt
  Comparator #(.width(4)) comparator_14 (.a(in_9[23:20]), .b(SS_L), .eq(comparator_14_eq));  // open: gt, lt
  and and_17 (and_17_out, comparator_9_eq, comparator_10_eq, comparator_11_eq, comparator_12_eq, comparator_13_eq, comparator_14_eq);
  // Buzzer buzzer_1: pin names not known; wires that end beside it: and_17_out

  // Other names for the same wires on the sheet: H0[3:0] = HH_L; H1[3:0] = HH_H; M0[3:0] = MM_L; M1[3:0] = MM_H;
  //   S0[3:0] = SS_L; S1[3:0] = SS_H

  // Notes on the sheet:
  //   设置初始时间BCD码
  //   输入信号
  //   请勿修改引脚名称、电路名称及电路封装外观
  //   数字时钟
  //   提示：使用4位二进制加法计数器子电路、比较器和独立逻辑门组件实现数字时钟。
  //   在载入有效时，检测设置数据错误
  //   生成三色LED显示信号，持续10个时钟周期
endmodule
