// Logisim project 快速乘法器.circ as structural Verilog: 4 circuits, main circuit 32bit
module main (
  input  [3:0] in_1,
  input  [3:0] in_2,
  output [7:0] out_3
);

  wire adder_2_cout, adder_2_out, adder_3_cout, adder_4_cout, adder_4_out, adder_5_cout, adder_6_cout,
       adder_6_out, adder_7_cout, adder_7_out, adder_8_cout, adder_8_out, adder_9_cout, adder_10_cout,
       adder_10_out, adder_11_cout, adder_12_cout, x0y1, x0y2, x0y3, x1y0, x1y1, x1y2, x1y3, x2y0, x2y1,
       x2y2, x2y3, x3y0, x3y1, x3y2, x3y3;

  Adder #(.width(1)) adder_1 (.a(adder_2_cout), .b(x3y3), .out(out_3[6]), .cin(adder_3_cout), .cout(out_3[7]));
  Adder #(.width(1)) adder_2 (.a(adder_6_cout), .b(x3y2), .out(adder_2_out), .cin(adder_4_cout), .cout(adder_2_cout));
  Adder #(.width(1)) adder_3 (.a(adder_2_out), .b(x2y3), .out(out_3[5]), .cin(adder_5_cout), .cout(adder_3_cout));
  Adder #(.width(1)) adder_4 (.a(adder_6_out), .b(x2y2), .out(adder_4_out), .cin(adder_8_cout), .cout(adder_4_cout));
  Adder #(.width(1)) adder_5 (.a(adder_4_out), .b(x1y3), .out(out_3[4]), .cin(adder_9_cout), .cout(adder_5_cout));
  and and_1 (x3y0, in_2[0], in_1[3]);
  and and_2 (x3y1, in_2[1], in_1[3]);
  and and_3 (x3y2, in_2[2], in_1[3]);
  and and_4 (x3y3, in_2[3], in_1[3]);
  Adder #(.width(1)) adder_6 (.a(1'b0), .b(x3y1), .out(adder_6_out), .cin(adder_7_cout), .cout(adder_6_cout));
  Adder #(.width(1)) adder_7 (.a(x3y0), .b(x2y1), .out(adder_7_out), .cin(adder_10_cout), .cout(adder_7_cout));
  Adder #(.width(1)) adder_8 (.a(adder_7_out), .b(x1y2), .out(adder_8_out), .cin(adder_11_cout), .cout(adder_8_cout));
  Adder #(.width(1)) adder_9 (.a(adder_8_out), .b(x0y3), .out(out_3[3]), .cin(1'b0), .cout(adder_9_cout));
  and and_5 (x2y0, in_2[0], in_1[2]);
  and and_6 (x2y1, in_2[1], in_1[2]);
  and and_7 (x2y2, in_2[2], in_1[2]);
  and and_8 (x2y3, in_2[3], in_1[2]);
  Adder #(.width(1)) adder_10 (.a(x2y0), .b(x1y1), .out(adder_10_out), .cin(adder_12_cout), .cout(adder_10_cout));
  Adder #(.width(1)) adder_11 (.a(adder_10_out), .b(x0y2), .out(out_3[2]), .cin(1'b0), .cout(adder_11_cout));
  and and_9 (x1y0, in_2[0], in_1[1]);
  and and_10 (x1y1, in_2[1], in_1[1]);
  and and_11 (x1y2, in_2[2], in_1[1]);
  and and_12 (x1y3, in_2[3], in_1[1]);
  Adder #(.width(1)) adder_12 (.a(x1y0), .b(x0y1), .out(out_3[1]), .cin(1'b0), .cout(adder_12_cout));
  and and_13 (out_3[0], in_2[0], in_1[0]);
  and and_14 (x0y1, in_2[1], in_1[0]);
  and and_15 (x0y2, in_2[2], in_1[0]);
  and and_16 (x0y3, in_2[3], in_1[0]);

  // Other names for the same wires on the sheet: F[7:0] = out_3; x0y0 = out_3[0]; x0 = in_1[0]; x1 = in_1[1];
  //   x2 = in_1[2]; x3 = in_1[3]; y0 = in_2[0]; y1 = in_2[1]; y2 = in_2[2]; y3 = in_2[3]
endmodule

module _8bit (
  input  [7:0] in_1,
  input  [7:0] in_2,
  output [15:0] out_3
);

  wire [7:0] main_1_out_3, main_2_out_3, main_3_out_3, main_4_out_3;
  wire [11:0] adder_1_out;
  wire [15:4] adder_2_out;

  main main_1 (.out_3(main_1_out_3), .in_1(in_2[3:0]), .in_2(in_1[3:0]));
  main main_2 (.out_3(main_2_out_3), .in_1(in_2[3:0]), .in_2(in_1[7:4]));
  main main_3 (.out_3(main_3_out_3), .in_1(in_2[7:4]), .in_2(in_1[3:0]));
  main main_4 (.out_3(main_4_out_3), .in_1(in_2[7:4]), .in_2(in_1[7:4]));
  Adder #(.width(12)) adder_1 (
    .a({4'b0000, main_1_out_3}), .b({main_2_out_3, 4'b0000}), .out(adder_1_out));  // open: cin, cout
  Adder #(.width(12)) adder_2 (
    .a({4'b0000, main_3_out_3}), .b({main_4_out_3, 4'b0000}), .out(adder_2_out));  // open: cin, cout
  Adder #(.width(16)) adder_3 (.a({4'b0000, adder_1_out}), .b({adder_2_out, 4'b0000}), .out(out_3));  // open: cin, cout
endmodule

module _16bit (
  input  [15:0] in_1,
  input  [15:0] in_2,
  output [31:0] out_3
);

  wire [15:0] n8bit_1_out_3, n8bit_3_out_3;
  wire [23:0] adder_1_out, adder_2_out;
  wire [23:8] n8bit_2_out_3, n8bit_4_out_3;

  _8bit u_8bit_1 (.in_1(in_1[7:0]), .in_2(in_2[7:0]), .out_3(n8bit_1_out_3));
  _8bit u_8bit_2 (.in_1(in_1[15:8]), .in_2(in_2[7:0]), .out_3(n8bit_2_out_3));
  _8bit u_8bit_3 (.in_1(in_1[7:0]), .in_2(in_2[15:8]), .out_3(n8bit_3_out_3));
  _8bit u_8bit_4 (.in_1(in_1[15:8]), .in_2(in_2[15:8]), .out_3(n8bit_4_out_3));
  Adder #(.width(24)) adder_1 (
    .a({{8{1'b0}}, n8bit_1_out_3}), .b({n8bit_2_out_3, {8{1'b0}}}), .out(adder_1_out));  // open: cin, cout
  Adder #(.width(24)) adder_2 (
    .a({{8{1'b0}}, n8bit_3_out_3}), .b({n8bit_4_out_3, {8{1'b0}}}), .out(adder_2_out));  // open: cin, cout
  Adder #(.width(32)) adder_3 (
    .a({{8{1'b0}}, adder_1_out}), .b({adder_2_out, {8{1'b0}}}), .out(out_3));  // open: cin, cout
endmodule

module _32bit (
  input  [31:0] in_1,
  input  [31:0] in_2,
  output out_3,
  output [31:0] out_4
);

  wire adder_1_cout, and_1_out, comparator_1_eq, comparator_2_eq, not_1_out;
  wire [15:0] n16bit_1_out_3, n16bit_1_out_3_2, n16bit_3_out_3;
  wire [31:0] main_1_s, main_2_s, n16bit_2_out_3, n16bit_4_out_3;
  wire [31:16] n16bit_3_out_3_2;

  _16bit u_16bit_1 (.in_1(in_1[15:0]), .in_2(in_2[15:0]), .out_3({n16bit_1_out_3, n16bit_1_out_3_2}));
  _16bit u_16bit_2 (.in_1(in_1[31:16]), .in_2(in_2[15:0]), .out_3(n16bit_2_out_3));
  _16bit u_16bit_3 (.in_1(in_1[15:0]), .in_2(in_2[31:16]), .out_3({n16bit_3_out_3, n16bit_3_out_3_2}));
  _16bit u_16bit_4 (.in_1(in_1[31:16]), .in_2(in_2[31:16]), .out_3(n16bit_4_out_3));
  lab4_3_main main_1 (
    .X({{16{1'b0}}, n16bit_1_out_3}), .Y(n16bit_2_out_3), .S(main_1_s));  // open: Cin, Cout, OF, CF, ZF, SF
  lab4_3_main main_2 (
    .X({{16{1'b0}}, n16bit_3_out_3}), .Y(n16bit_4_out_3), .S(main_2_s));  // open: Cin, Cout, OF, CF, ZF, SF
  Comparator #(.width(16)) comparator_1 (.a(main_1_s[31:16]), .b({16{1'b0}}), .eq(comparator_1_eq));  // open: gt, lt
  Comparator #(.width(32), .mode("unsigned")) comparator_2 (
    .a(main_2_s), .b({32{1'b0}}), .eq(comparator_2_eq));  // open: gt, lt
  not not_1 (not_1_out, adder_1_cout);
  and and_1 (and_1_out, comparator_1_eq, comparator_2_eq, not_1_out);
  not not_2 (out_3, and_1_out);
  Adder #(.width(32)) adder_1 (
    .a({main_1_s[15:0], n16bit_1_out_3_2}), .b({n16bit_3_out_3_2, {16{1'b0}}}), .out(out_4),
    .cout(adder_1_cout));  // open: cin

  // Other names for the same wires on the sheet: overflow = out_3
endmodule
