// Logisim project lab4.3.circ as structural Verilog: 1 circuit, main circuit main
// 加法器
module main (
  input  Cin,
  input  [31:0] X,
  input  [31:0] Y,
  output OF,
  output Cout,
  output CF,
  output ZF,
  output [31:0] S,
  output SF
);

  wire and_1_out, and_2_out, and_3_out, and_4_out, main_2_c16, nor_1_out, nor_2_out, nor_3_out, nor_4_out,
       nor_5_out, nor_6_out, nor_7_out, nor_8_out, not_1_out, not_2_out, not_3_out;

  and and_1 (and_1_out, X[31], Y[31], not_3_out);
  lab4_2_main main_1 (.X(X[31:16]), .Y(Y[31:16]), .C0(main_2_c16), .S(S[31:16]), .C16(Cout));  // open: Pg, Gg
  not not_1 (not_1_out, X[31]);
  lab4_2_main main_2 (.X(X[15:0]), .Y(Y[15:0]), .C0(Cin), .S(S[15:0]), .C16(main_2_c16));  // open: Pg, Gg
  not not_2 (not_2_out, Y[31]);
  and and_2 (and_2_out, not_1_out, not_2_out, S[31]);
  not not_3 (not_3_out, S[31]);
  or or_1 (OF, and_2_out, and_1_out);
  // Probe on X
  // Probe on Y
  // Probe on S
  xor xor_1 (CF, Cin, Cout);
  nor nor_1 (nor_1_out, S[0], S[1], S[2], S[3]);
  nor nor_2 (nor_2_out, S[4], S[5], S[6], S[7]);
  nor nor_3 (nor_3_out, S[8], S[9], S[10], S[11]);
  nor nor_4 (nor_4_out, S[12], S[13], S[14], S[15]);
  nor nor_5 (nor_5_out, S[16], S[17], S[18], S[19]);
  nor nor_6 (nor_6_out, S[20], S[21], S[22], S[23]);
  nor nor_7 (nor_7_out, S[24], S[25], S[26], S[27]);
  nor nor_8 (nor_8_out, S[28], S[29], S[30], S[31]);
  and and_3 (and_3_out, nor_1_out, nor_2_out, nor_3_out, nor_4_out);
  and and_4 (and_4_out, nor_5_out, nor_6_out, nor_7_out, nor_8_out);
  and and_5 (ZF, and_3_out, and_4_out);

  assign SF = S[31];

  // Notes on the sheet:
  //   Y: pull=down
  //   X: pull=down
  //   Cin: pull=down
  //   输入引脚区
  //   输出引脚区
  //   请勿修改引脚名称、电路名称及电路封装外观
  //   提示：使用两个16位并行加法器子电路串行实现32位快速加法器
  //   功能说明:32位Adder  S=X+Y，Cout为最高位进位位，Cin为进位输入， S为和，溢出OF、进位CF、零ZF、符号SF。
  //   +
  //   =
  //   无符号加法
endmodule
