// Logisim project lab4.5.circ as structural Verilog: 5 circuits, main circuit ALU
module ALU (
  input  [3:0] ALUctr,
  input  [31:0] A,
  input  [31:0] B,
  output Zero,
  output out_5,
  output [31:0] S
);

  wire aluctrl_1_alctr, aluctrl_1_sftctr, aluctrl_1_sigctr, aluctrl_1_subctr, main_2_cf, main_2_of,
       main_2_sf, multiplexer_2_out, xor_3_out;
  wire [2:0] aluctrl_1_opctr;
  wire [4:0] b_4_0_1_out_2;
  wire [31:0] and_1_out, ext_of_subctr_1_out_2, main_1_dataout, main_2_s, n32bit_1_out_4, or_1_out,
       xor_1_out, xor_2_out, zero_extention_1_out_2;

  Ext_of_SUBctr ext_of_subctr_1 (.in_1(aluctrl_1_subctr), .out_2(ext_of_subctr_1_out_2));
  B_4_0 b_4_0_1 (.in_1(B), .out_2(b_4_0_1_out_2));
  _32bit u_32bit_1 (.in_1(A), .in_2(B), .out_3(out_5), .out_4(n32bit_1_out_4));
  assign xor_1_out = B ^ ext_of_subctr_1_out_2;  // XOR_Gate xor_1, 32 bits wide
  assign and_1_out = A & B;  // AND_Gate and_1, 32 bits wide
  assign or_1_out = A | B;  // OR_Gate or_1, 32 bits wide
  assign xor_2_out = A ^ B;  // XOR_Gate xor_2, 32 bits wide
  lab4_4_main main_1 (
    .L_R(aluctrl_1_sftctr), .shamt(b_4_0_1_out_2), .DataIn(A), .DataOut(main_1_dataout), .A_L(aluctrl_1_alctr));
  lab4_3_main main_2 (
    .Cin(aluctrl_1_subctr), .X(A), .Y(xor_1_out), .S(main_2_s), .OF(main_2_of), .CF(main_2_cf), .ZF(Zero),
    .SF(main_2_sf));  // open: Cout
  xor xor_3 (xor_3_out, main_2_of, main_2_sf);
  ALUctrl aluctrl_1 (
    .ALUctr(ALUctr), .SUBctr(aluctrl_1_subctr), .SFTctr(aluctrl_1_sftctr), .SIGctr(aluctrl_1_sigctr),
    .ALctr(aluctrl_1_alctr), .OPctr(aluctrl_1_opctr));
  Multiplexer #(.select(3), .width(32), .enable("false")) multiplexer_1 (
    .in0(main_2_s), .in1(and_1_out), .in2(or_1_out), .in3(xor_2_out), .in4(main_1_dataout), .in5(B),
    .in6(zero_extention_1_out_2), .in7(n32bit_1_out_4), .out(S), .sel(aluctrl_1_opctr));
  // Probe on A
  // Probe on B
  // Probe on S
  Multiplexer #(.enable("false")) multiplexer_2 (
    .in0(main_2_cf), .in1(xor_3_out), .out(multiplexer_2_out), .sel(aluctrl_1_sigctr));
  Zero_Extention zero_extention_1 (.in_1(multiplexer_2_out), .out_2(zero_extention_1_out_2));

  // Other names for the same wires on the sheet: muloverflow = out_5; Result[31:0] = S

  // Notes on the sheet:
  //   A: pull=down
  //   ALUctr: pull=down
  //   B: pull=down
  //   输入引脚
  //   请勿修改引脚名称、电路名称及电路封装外观
  //   提示：使用32位并行加法器子电路、桶形移位器、ALU控制子电路实现32位ALU
  //   功能说明:32位ALU，输入32位操作数A、B，4位控制信号ALUctr，输出32位结果Reseult和1位Zero标志位
  //   输出引脚
  //   操作数和结果
endmodule

// ALU操作控制信号
module ALUctrl (
  input  [3:0] ALUctr,
  output SUBctr,
  output SFTctr,
  output SIGctr,
  output ALctr,
  output [2:0] OPctr
);

  wire and_2_out, and_3_out, and_6_out, and_7_out, and_8_out, and_9_out, and_10_out, and_11_out, not_1_out,
       not_2_out, not_3_out, not_4_out;

  not not_1 (not_1_out, ALUctr[0]);
  not not_2 (not_2_out, ALUctr[1]);
  not not_3 (not_3_out, ALUctr[2]);
  not not_4 (not_4_out, ALUctr[3]);
  and and_1 (SIGctr, not_1_out, ALUctr[1], not_3_out, not_4_out);
  and and_2 (and_2_out, ALUctr[0], ALUctr[1], not_3_out, not_4_out);
  and and_3 (and_3_out, not_1_out, not_2_out, not_3_out, ALUctr[3]);
  and and_4 (ALctr, ALUctr[0], not_2_out, ALUctr[2], ALUctr[3]);
  and and_5 (SFTctr, not_3_out, not_4_out, not_2_out, ALUctr[0]);
  and and_6 (and_6_out, not_1_out, not_2_out, ALUctr[2], not_4_out);
  and and_7 (and_7_out, ALUctr[0], ALUctr[1], ALUctr[2], not_4_out);
  and and_8 (and_8_out, ALUctr[0], ALUctr[1], ALUctr[2], ALUctr[3]);
  and and_9 (and_9_out, not_1_out, ALUctr[1], ALUctr[2], not_4_out);
  and and_10 (and_10_out, ALUctr[0], not_2_out, ALUctr[2], not_4_out);
  and and_11 (and_11_out, not_1_out, ALUctr[1], ALUctr[2], ALUctr[3]);
  or or_1 (SUBctr, SIGctr, and_2_out, and_3_out);
  or or_2 (OPctr[0], and_6_out, and_7_out, and_8_out, and_11_out);
  or or_3 (OPctr[1], SIGctr, and_2_out, and_11_out, and_6_out, and_9_out);
  or or_4 (OPctr[2], SFTctr, SIGctr, and_2_out, and_11_out, and_10_out, ALctr, and_8_out);

  // Other names for the same wires on the sheet: LRctr = SFTctr

  // Notes on the sheet:
  //   输入引脚
  //   ALU操作控制信号生成部件
  //   输出引脚
endmodule

module Ext_of_SUBctr (
  input  in_1,
  output [31:0] out_2
);


  assign out_2 = {32{in_1}};
endmodule

module B_4_0 (
  input  [31:0] in_1,
  output [4:0] out_2
);


  assign out_2 = in_1[4:0];
endmodule

module Zero_Extention (
  input  in_1,
  output [31:0] out_2
);


  assign out_2 = {{31{1'b0}}, in_1};
endmodule
