// Logisim project 除法器.circ as structural Verilog: 1 circuit, main circuit main
module main (
  input  [31:0] in_1,
  input  [31:0] in_2,
  input  [31:0] in_3,
  output [31:0] out_4,
  output [31:0] out_5
);

  wire clock_1_out, comparator_1_eq, comparator_2_eq;
  wire [0:0] not_1_out;
  wire [7:0] counter_1_q;
  wire [31:0] adder_1_out, adder_2_out, adder_3_out, multiplexer_1_out, multiplexer_2_out, multiplexer_3_out,
       multiplexer_4_out, multiplexer_5_out, negator_1_out;

  Clock clock_1 (.out(clock_1_out));
  Adder #(.width(32)) adder_1 (.a(out_5), .b(in_3), .out(adder_1_out));  // open: cin, cout
  // Probe on in_1
  // Probe on in_2
  // Probe on in_3
  Negator #(.width(32)) negator_1 (.in(in_3), .out(negator_1_out));
  Multiplexer #(.width(32), .enable("false")) multiplexer_1 (
    .in0(adder_2_out), .in1(multiplexer_2_out), .out(multiplexer_1_out), .sel(comparator_1_eq));
  Multiplexer #(.width(32), .enable("false")) multiplexer_2 (
    .in0(out_5), .in1(adder_1_out), .out(multiplexer_2_out), .sel(out_5[31]));
  Counter counter_1 (.D({8{1'b0}}), .Q(counter_1_q), .clk(clock_1_out));  // open: load, count, carry, clr, preset, down
  Multiplexer #(.width(32), .enable("false")) multiplexer_3 (
    .in0(negator_1_out), .in1(in_3), .out(multiplexer_3_out), .sel(out_5[31]));
  Comparator #(.mode("unsigned")) comparator_1 (.a(counter_1_q), .b(8'h21), .eq(comparator_1_eq));  // open: gt, lt
  Comparator #(.mode("unsigned")) comparator_2 (.a(counter_1_q), .b({8{1'b0}}), .eq(comparator_2_eq));  // open: gt, lt
  Adder #(.width(32)) adder_2 (
    .a({out_5[30:0], out_4[31]}), .b(multiplexer_3_out), .out(adder_2_out));  // open: cin, cout
  Adder #(.width(32)) adder_3 (.a(in_1), .b(negator_1_out), .out(adder_3_out));  // open: cin, cout
  Multiplexer #(.width(32), .enable("false")) multiplexer_4 (
    .in0(multiplexer_1_out), .in1(adder_3_out), .out(multiplexer_4_out), .sel(comparator_2_eq));
  Register #(.width(32), .Select("low")) register_1 (
    .D(multiplexer_4_out), .Q(out_5), .clk(clock_1_out));  // open: en, clr
  // Probe on out_5
  Register #(.width(32), .Select("low")) register_2 (
    .D(multiplexer_5_out), .Q(out_4), .clk(clock_1_out));  // open: en, clr
  // Probe on out_4
  not not_1 (not_1_out[0], out_5[31]);
  Multiplexer #(.width(32), .enable("false")) multiplexer_5 (
    .in0({out_4[30:0], not_1_out[0]}), .in1(in_2), .out(multiplexer_5_out), .sel(comparator_2_eq));
endmodule
