// Logisim project lab5.2.circ as structural Verilog: 1 circuit, main circuit DataRam
// DataRAM
module DataRam (
  input  CLK,
  input  CLR,
  input  WE,
  input  [2:0] MemOp,
  input  [17:0] Addr,
  input  [31:0] Din,
  output AlignErr,
  output [31:0] DataOut
);

  wire and_1_out, and_2_out, and_3_out, and_4_out, and_5_out, and_6_out, and_7_out, and_8_out, and_9_out,
       and_10_out, and_11_out, and_12_out, and_13_out, and_14_out, and_15_out, not_1_out, not_2_out,
       not_3_out, not_4_out, not_5_out;
  wire [3:0] SEL;
  wire [7:0] multiplexer_1_out, multiplexer_3_out, multiplexer_4_out, multiplexer_6_out, multiplexer_7_out,
       multiplexer_9_out, ram_1_data, ram_2_data, ram_3_data, ram_4_data;

  Multiplexer #(.select(4), .width(8), .enable("false")) multiplexer_1 (
    .in8(Din[7:0]), .in12(Din[15:8]), .in15(Din[31:24]), .out(multiplexer_1_out), .sel(SEL));  // open: in0, in1, in2, in3, in4, in5, in6, in7, in9, in10, in11, in13, in14
  Multiplexer #(.select(4), .width(8), .enable("false")) multiplexer_2 (
    .in1(multiplexer_6_out), .in2(multiplexer_6_out), .in3(multiplexer_3_out), .in4(multiplexer_6_out),
    .in8(multiplexer_6_out), .in12(multiplexer_3_out), .in15(ram_1_data), .out(DataOut[31:24]), .sel(SEL));  // open: in0, in5, in6, in7, in9, in10, in11, in13, in14
  RAM #(.addrWidth(16), .bus("separate"), .Select("high")) ram_1 (
    .addr(Addr[17:2]), .din(multiplexer_1_out), .data(ram_1_data), .str(WE), .sel(SEL[3]), .clk(CLK),
    .ld(1'b1), .clr(CLR));
  Multiplexer #(.width(8), .enable("false")) multiplexer_3 (
    .in0({8{1'b0}}), .in1({8{DataOut[15]}}), .out(multiplexer_3_out), .sel(MemOp[2]));
  Multiplexer #(.select(4), .width(8), .enable("false")) multiplexer_4 (
    .in4(Din[7:0]), .in12(Din[7:0]), .in15(Din[23:16]), .out(multiplexer_4_out), .sel(SEL));  // open: in0, in1, in2, in3, in5, in6, in7, in8, in9, in10, in11, in13, in14
  Multiplexer #(.select(4), .width(8), .enable("false")) multiplexer_5 (
    .in1(multiplexer_6_out), .in2(multiplexer_6_out), .in3(multiplexer_3_out), .in4(multiplexer_6_out),
    .in8(multiplexer_6_out), .in12(multiplexer_3_out), .in15(ram_2_data), .out(DataOut[23:16]), .sel(SEL));  // open: in0, in5, in6, in7, in9, in10, in11, in13, in14
  RAM #(.addrWidth(16), .bus("separate"), .Select("high")) ram_2 (
    .addr(Addr[17:2]), .din(multiplexer_4_out), .data(ram_2_data), .str(WE), .sel(SEL[2]), .clk(CLK),
    .ld(1'b1), .clr(CLR));
  Multiplexer #(.width(8), .enable("false")) multiplexer_6 (
    .in0({8{1'b0}}), .in1({8{DataOut[7]}}), .out(multiplexer_6_out), .sel(MemOp[2]));
  Multiplexer #(.select(4), .width(8), .enable("false")) multiplexer_7 (
    .in2(Din[7:0]), .in3(Din[15:8]), .in15(Din[15:8]), .out(multiplexer_7_out), .sel(SEL));  // open: in0, in1, in4, in5, in6, in7, in8, in9, in10, in11, in12, in13, in14
  Multiplexer #(.select(4), .width(8), .enable("false")) multiplexer_8 (
    .in1(multiplexer_6_out), .in2(multiplexer_6_out), .in3(ram_3_data), .in4(multiplexer_6_out),
    .in8(multiplexer_6_out), .in12(ram_1_data), .in15(ram_3_data), .out(DataOut[15:8]), .sel(SEL));  // open: in0, in5, in6, in7, in9, in10, in11, in13, in14
  RAM #(.addrWidth(16), .bus("separate"), .Select("high")) ram_3 (
    .addr(Addr[17:2]), .din(multiplexer_7_out), .data(ram_3_data), .str(WE), .sel(SEL[1]), .clk(CLK),
    .ld(1'b1), .clr(CLR));
  Multiplexer #(.select(4), .width(8), .enable("false")) multiplexer_9 (
    .in1(Din[7:0]), .in3(Din[7:0]), .in15(Din[7:0]), .out(multiplexer_9_out), .sel(SEL));  // open: in0, in2, in4, in5, in6, in7, in8, in9, in10, in11, in12, in13, in14
  Multiplexer #(.select(4), .width(8), .enable("false")) multiplexer_10 (
    .in1(ram_4_data), .in2(ram_3_data), .in3(ram_4_data), .in4(ram_2_data), .in8(ram_1_data),
    .in12(ram_2_data), .in15(ram_4_data), .out(DataOut[7:0]), .sel(SEL));  // open: in0, in5, in6, in7, in9, in10, in11, in13, in14
  RAM #(.addrWidth(16), .bus("separate"), .Select("high")) ram_4 (
    .addr(Addr[17:2]), .din(multiplexer_9_out), .data(ram_4_data), .str(WE), .sel(SEL[0]), .clk(CLK),
    .ld(1'b1), .clr(CLR));
  not not_1 (not_1_out, MemOp[2]);
  not not_2 (not_2_out, MemOp[1]);
  not not_3 (not_3_out, MemOp[0]);
  not not_4 (not_4_out, Addr[1]);
  not not_5 (not_5_out, Addr[0]);
  and and_1 (and_1_out, MemOp[2], not_2_out, not_3_out);
  and and_2 (and_2_out, not_2_out, not_3_out, not_4_out, Addr[0]);
  and and_3 (and_3_out, not_2_out, not_3_out, Addr[1], not_5_out);
  and and_4 (and_4_out, not_2_out, not_3_out, Addr[0], Addr[1]);
  and and_5 (and_5_out, MemOp[1], not_3_out, not_4_out, Addr[0]);
  and and_6 (and_6_out, MemOp[1], not_3_out, Addr[1], Addr[0]);
  and and_7 (and_7_out, MemOp[1], MemOp[0]);
  and and_8 (and_8_out, not_1_out, not_2_out, not_3_out, not_4_out, not_5_out);
  and and_9 (and_9_out, not_2_out, MemOp[0], not_4_out, not_5_out);
  and and_10 (and_10_out, MemOp[1], not_3_out, not_4_out, not_5_out);
  and and_11 (and_11_out, not_2_out, MemOp[0], not_4_out, Addr[0]);
  and and_12 (and_12_out, MemOp[1], not_3_out, not_4_out, not_5_out);
  and and_13 (and_13_out, not_2_out, MemOp[0], Addr[1], not_5_out);
  and and_14 (and_14_out, MemOp[1], not_3_out, Addr[1], not_5_out);
  and and_15 (and_15_out, not_2_out, MemOp[0], Addr[1], Addr[0]);
  or or_1 (AlignErr, and_2_out, and_3_out, and_4_out, and_1_out, and_5_out, and_6_out, and_7_out);
  or or_2 (SEL[0], and_8_out, and_9_out, and_10_out);
  or or_3 (SEL[1], and_8_out, and_11_out, and_12_out);
  or or_4 (SEL[2], and_8_out, and_13_out, and_14_out);
  or or_5 (SEL[3], and_8_out, and_14_out, and_15_out);

  // Other names for the same wires on the sheet: Dout[31:0] = DataOut

  // Notes on the sheet:
  //   输入引脚
  //   请勿修改引脚名称、电路名称及电路封装外观
  //   为了后续实验中的引用，不要修改MemOp的编码定义、引脚名称和在布局中的位置。
  //   32位数据存储器，按字节分4片存储，可按照字节、半字和字进行存储；读取字节或半字时，支持0扩展和符号位扩展。
  //   输出引脚
endmodule
