// Logisim project 显示器.circ as structural Verilog: 1 circuit, main circuit main
module main (
);

  wire clock_1_out, comparator_1_eq;
  wire [2:0] counter_1_q;
  wire [6:0] multiplexer_1_out, multiplexer_2_out, multiplexer_3_out, multiplexer_4_out, multiplexer_5_out,
       multiplexer_6_out, multiplexer_7_out;
  wire [7:0] main_1_row1, main_1_row2, main_1_row3, main_1_row4, main_1_row5, main_1_row6, main_1_row7,
       main_1_row8, main_1_row9, main_1_row10, main_1_row11, main_1_row12, main_1_row13, main_1_row14,
       main_1_row15, main_1_row16, main_2_row1, main_2_row2, main_2_row3, main_2_row4, main_2_row5,
       main_2_row6, main_2_row7, main_2_row8, main_2_row9, main_2_row10, main_2_row11, main_2_row12,
       main_2_row13, main_2_row14, main_2_row15, main_2_row16, main_3_row1, main_3_row2, main_3_row3,
       main_3_row4, main_3_row5, main_3_row6, main_3_row7, main_3_row8, main_3_row9, main_3_row10,
       main_3_row11, main_3_row12, main_3_row13, main_3_row14, main_3_row15, main_3_row16, main_4_row1,
       main_4_row2, main_4_row3, main_4_row4, main_4_row5, main_4_row6, main_4_row7, main_4_row8,
       main_4_row9, main_4_row10, main_4_row11, main_4_row12, main_4_row13, main_4_row14, main_4_row15,
       main_4_row16, main_5_row1, main_5_row2, main_5_row3, main_5_row4, main_5_row5, main_5_row6,
       main_5_row7, main_5_row8, main_5_row9, main_5_row10, main_5_row11, main_5_row12, main_5_row13,
       main_5_row14, main_5_row15, main_5_row16, main_6_row1, main_6_row2, main_6_row3, main_6_row4,
       main_6_row5, main_6_row6, main_6_row7, main_6_row8, main_6_row9, main_6_row10, main_6_row11,
       main_6_row12, main_6_row13, main_6_row14, main_6_row15, main_6_row16, main_7_row1, main_7_row2,
       main_7_row3, main_7_row4, main_7_row5, main_7_row6, main_7_row7, main_7_row8, main_7_row9,
       main_7_row10, main_7_row11, main_7_row12, main_7_row13, main_7_row14, main_7_row15, main_7_row16;

  Counter #(.width(3), .max('h7)) counter_1 (
    .Q(counter_1_q), .clk(clock_1_out), .clr(comparator_1_eq));  // open: load, D, count, carry, preset, down
  Clock clock_1 (.out(clock_1_out));
  Multiplexer #(.select(3), .width(7), .enable("false")) multiplexer_1 (
    .in0(7'b1001110), .in1(7'b1001010), .in2(7'b1010101), .in3(7'b1000011), .in4(7'b1010011),
    .in5(7'b0100000), .in6(7'b0100000), .out(multiplexer_1_out), .sel(counter_1_q));  // open: in7
  DotMatrix #(.inputtype("row"), .matrixcols(8), .matrixrows(16)) dotmatrix_1 (
    .row0(main_1_row1), .row1(main_1_row2), .row2(main_1_row3), .row3(main_1_row4), .row4(main_1_row5),
    .row5(main_1_row6), .row6(main_1_row7), .row7(main_1_row8), .row8(main_1_row9), .row9(main_1_row10),
    .row10(main_1_row11), .row11(main_1_row12), .row12(main_1_row13), .row13(main_1_row14),
    .row14(main_1_row15), .row15(main_1_row16));
  lab5_1_main main_1 (
    .ASCII_CODE(multiplexer_1_out), .row1(main_1_row1), .row2(main_1_row2), .row3(main_1_row3),
    .row4(main_1_row4), .row7(main_1_row7), .row5(main_1_row5), .row6(main_1_row6), .row8(main_1_row8),
    .row9(main_1_row9), .row10(main_1_row10), .row11(main_1_row11), .row12(main_1_row12),
    .row13(main_1_row13), .row14(main_1_row14), .row15(main_1_row15), .row16(main_1_row16));  // open: CodeErr
  Comparator #(.width(3)) comparator_1 (.a(counter_1_q), .b(3'b111), .eq(comparator_1_eq));  // open: gt, lt
  Multiplexer #(.select(3), .width(7), .enable("false")) multiplexer_2 (
    .in0(7'b1001010), .in1(7'b1010101), .in2(7'b1000011), .in3(7'b1010011), .in4(7'b0100000),
    .in5(7'b0100000), .in6(7'b1001110), .out(multiplexer_2_out), .sel(counter_1_q));  // open: in7
  lab5_1_main main_2 (
    .ASCII_CODE(multiplexer_2_out), .row1(main_2_row1), .row2(main_2_row2), .row3(main_2_row3),
    .row4(main_2_row4), .row7(main_2_row7), .row5(main_2_row5), .row6(main_2_row6), .row8(main_2_row8),
    .row9(main_2_row9), .row10(main_2_row10), .row11(main_2_row11), .row12(main_2_row12),
    .row13(main_2_row13), .row14(main_2_row14), .row15(main_2_row15), .row16(main_2_row16));  // open: CodeErr
  DotMatrix #(.inputtype("row"), .matrixcols(8), .matrixrows(16)) dotmatrix_2 (
    .row0(main_2_row1), .row1(main_2_row2), .row2(main_2_row3), .row3(main_2_row4), .row4(main_2_row5),
    .row5(main_2_row6), .row6(main_2_row7), .row7(main_2_row8), .row8(main_2_row9), .row9(main_2_row10),
    .row10(main_2_row11), .row11(main_2_row12), .row12(main_2_row13), .row13(main_2_row14),
    .row14(main_2_row15), .row15(main_2_row16));
  Multiplexer #(.select(3), .width(7), .enable("false")) multiplexer_3 (
    .in0(7'b1010101), .in1(7'b1000011), .in2(7'b1010011), .in3(7'b0100000), .in4(7'b0100000),
    .in5(7'b1001110), .in6(7'b1001010), .out(multiplexer_3_out), .sel(counter_1_q));  // open: in7
  DotMatrix #(.inputtype("row"), .matrixcols(8), .matrixrows(16)) dotmatrix_3 (
    .row0(main_3_row1), .row1(main_3_row2), .row2(main_3_row3), .row3(main_3_row4), .row4(main_3_row5),
    .row5(main_3_row6), .row6(main_3_row7), .row7(main_3_row8), .row8(main_3_row9), .row9(main_3_row10),
    .row10(main_3_row11), .row11(main_3_row12), .row12(main_3_row13), .row13(main_3_row14),
    .row14(main_3_row15), .row15(main_3_row16));
  lab5_1_main main_3 (
    .ASCII_CODE(multiplexer_3_out), .row1(main_3_row1), .row2(main_3_row2), .row3(main_3_row3),
    .row4(main_3_row4), .row7(main_3_row7), .row5(main_3_row5), .row6(main_3_row6), .row8(main_3_row8),
    .row9(main_3_row9), .row10(main_3_row10), .row11(main_3_row11), .row12(main_3_row12),
    .row13(main_3_row13), .row14(main_3_row14), .row15(main_3_row15), .row16(main_3_row16));  // open: CodeErr
  Multiplexer #(.select(3), .width(7), .enable("false")) multiplexer_4 (
    .in0(7'b1000011), .in1(7'b1010011), .in2(7'b0100000), .in3(7'b0100000), .in4(7'b1001110),
    .in5(7'b1001010), .in6(7'b1010101), .out(multiplexer_4_out), .sel(counter_1_q));  // open: in7
  lab5_1_main main_4 (
    .ASCII_CODE(multiplexer_4_out), .row1(main_4_row1), .row2(main_4_row2), .row3(main_4_row3),
    .row4(main_4_row4), .row7(main_4_row7), .row5(main_4_row5), .row6(main_4_row6), .row8(main_4_row8),
    .row9(main_4_row9), .row10(main_4_row10), .row11(main_4_row11), .row12(main_4_row12),
    .row13(main_4_row13), .row14(main_4_row14), .row15(main_4_row15), .row16(main_4_row16));  // open: CodeErr
  DotMatrix #(.inputtype("row"), .matrixcols(8), .matrixrows(16)) dotmatrix_4 (
    .row0(main_4_row1), .row1(main_4_row2), .row2(main_4_row3), .row3(main_4_row4), .row4(main_4_row5),
    .row5(main_4_row6), .row6(main_4_row7), .row7(main_4_row8), .row8(main_4_row9), .row9(main_4_row10),
    .row10(main_4_row11), .row11(main_4_row12), .row12(main_4_row13), .row13(main_4_row14),
    .row14(main_4_row15), .row15(main_4_row16));
  Multiplexer #(.select(3), .width(7), .enable("false")) multiplexer_5 (
    .in0(7'b1010011), .in1(7'b0100000), .in2(7'b0100000), .in3(7'b1001110), .in4(7'b1001010),
    .in5(7'b1010101), .in6(7'b1000011), .out(multiplexer_5_out), .sel(counter_1_q));  // open: in7
  lab5_1_main main_5 (
    .ASCII_CODE(multiplexer_5_out), .row1(main_5_row1), .row2(main_5_row2), .row3(main_5_row3),
    .row4(main_5_row4), .row7(main_5_row7), .row5(main_5_row5), .row6(main_5_row6), .row8(main_5_row8),
    .row9(main_5_row9), .row10(main_5_row10), .row11(main_5_row11), .row12(main_5_row12),
    .row13(main_5_row13), .row14(main_5_row14), .row15(main_5_row15), .row16(main_5_row16));  // open: CodeErr
  DotMatrix #(.inputtype("row"), .matrixcols(8), .matrixrows(16)) dotmatrix_5 (
    .row0(main_5_row1), .row1(main_5_row2), .row2(main_5_row3), .row3(main_5_row4), .row4(main_5_row5),
    .row5(main_5_row6), .row6(main_5_row7), .row7(main_5_row8), .row8(main_5_row9), .row9(main_5_row10),
    .row10(main_5_row11), .row11(main_5_row12), .row12(main_5_row13), .row13(main_5_row14),
    .row14(main_5_row15), .row15(main_5_row16));
  Multiplexer #(.select(3), .width(7), .enable("false")) multiplexer_6 (
    .in0(7'b0100000), .in1(7'b0100000), .in2(7'b1001110), .in3(7'b1001010), .in4(7'b1010101),
    .in5(7'b1000011), .in6(7'b1010011), .out(multiplexer_6_out), .sel(counter_1_q));  // open: in7
  lab5_1_main main_6 (
    .ASCII_CODE(multiplexer_6_out), .row1(main_6_row1), .row2(main_6_row2), .row3(main_6_row3),
    .row4(main_6_row4), .row7(main_6_row7), .row5(main_6_row5), .row6(main_6_row6), .row8(main_6_row8),
    .row9(main_6_row9), .row10(main_6_row10), .row11(main_6_row11), .row12(main_6_row12),
    .row13(main_6_row13), .row14(main_6_row14), .row15(main_6_row15), .row16(main_6_row16));  // open: CodeErr
  DotMatrix #(.inputtype("row"), .matrixcols(8), .matrixrows(16)) dotmatrix_6 (
    .row0(main_6_row1), .row1(main_6_row2), .row2(main_6_row3), .row3(main_6_row4), .row4(main_6_row5),
    .row5(main_6_row6), .row6(main_6_row7), .row7(main_6_row8), .row8(main_6_row9), .row9(main_6_row10),
    .row10(main_6_row11), .row11(main_6_row12), .row12(main_6_row13), .row13(main_6_row14),
    .row14(main_6_row15), .row15(main_6_row16));
  Multiplexer #(.select(3), .width(7), .enable("false")) multiplexer_7 (
    .in0(7'b0100000), .in1(7'b1001110), .in2(7'b1001010), .in3(7'b1010101), .in4(7'b1000011),
    .in5(7'b1010011), .in6(7'b0100000), .out(multiplexer_7_out), .sel(counter_1_q));  // open: in7
  lab5_1_main main_7 (
    .ASCII_CODE(multiplexer_7_out), .row1(main_7_row1), .row2(main_7_row2), .row3(main_7_row3),
    .row4(main_7_row4), .row7(main_7_row7), .row5(main_7_row5), .row6(main_7_row6), .row8(main_7_row8),
    .row9(main_7_row9), .row10(main_7_row10), .row11(main_7_row11), .row12(main_7_row12),
    .row13(main_7_row13), .row14(main_7_row14), .row15(main_7_row15), .row16(main_7_row16));  // open: CodeErr
  DotMatrix #(.inputtype("row"), .matrixcols(8), .matrixrows(16)) dotmatrix_7 (
    .row0(main_7_row1), .row1(main_7_row2), .row2(main_7_row3), .row3(main_7_row4), .row4(main_7_row5),
    .row5(main_7_row6), .row6(main_7_row7), .row7(main_7_row8), .row8(main_7_row9), .row9(main_7_row10),
    .row10(main_7_row11), .row11(main_7_row12), .row12(main_7_row13), .row13(main_7_row14),
    .row14(main_7_row15), .row15(main_7_row16));
endmodule
