// Logisim project lab6.1.circ as structural Verilog: 1 circuit, main circuit 控制器
module \控制器  (
  input  [6:0] opcode,
  input  [2:0] funct3,
  input  [6:0] funct7,
  output [2:0] ExtOp,
  output RegWr,
  output [2:0] Branch,
  output ALUASrc,
  output [1:0] ALUBSrc,
  output [3:0] ALUctr,
  output MemtoReg,
  output [2:0] MemOp,
  output MemWr,
  output Halt
);

  wire and_1_out, B_type, I_ALU, I_jalr, multiplexer_1_out, multiplexer_2_out, multiplexer_4_out,
       multiplexer_5_out, not_1_out, or_1_out, or_2_out, or_3_out, or_4_out, or_5_out, or_12_out, R_type,
       U_auipc, U_lui;
  wire [2:0] bit_extender_1_out, multiplexer_3_out, multiplexer_6_out, multiplexer_7_out, multiplexer_8_out,
       multiplexer_9_out, multiplexer_12_out, multiplexer_14_out;

  not not_1 (not_1_out, funct3[1]);
  and and_1 (and_1_out, funct3[0], not_1_out, funct3[2], funct7[5]);
  Multiplexer #(.enable("false")) multiplexer_1 (.in0(1'b0), .in1(1'b1), .out(multiplexer_1_out), .sel(and_1_out));
  Comparator #(.width(7), .mode("unsigned")) comparator_1 (.a(opcode), .b(7'b0110111), .eq(U_lui));  // open: gt, lt
  Comparator #(.width(7), .mode("unsigned")) comparator_2 (.a(opcode), .b(7'b1100111), .eq(I_jalr));  // open: gt, lt
  Multiplexer #(.enable("false")) multiplexer_2 (
    .in0(1'b0), .in1(multiplexer_1_out), .out(multiplexer_2_out), .sel(I_ALU));
  Comparator #(.width(7), .mode("unsigned")) comparator_3 (.a(opcode), .b(7'b0010111), .eq(U_auipc));  // open: gt, lt
  Comparator #(.width(7), .mode("unsigned")) comparator_4 (.a(opcode), .b(7'b1100011), .eq(B_type));  // open: gt, lt
  Multiplexer #(.select(3), .width(3), .disabled(0)) multiplexer_3 (
    .in0(3'b010), .in1(3'b010), .in4(3'b010), .in5(3'b010), .in6(3'b011), .in7(3'b011),
    .out(multiplexer_3_out), .sel(funct3), .en(B_type));  // open: in2, in3
  Multiplexer #(.enable("false")) multiplexer_4 (
    .in0(multiplexer_2_out), .in1(funct7[5]), .out(multiplexer_4_out), .sel(R_type));
  Multiplexer #(.enable("false")) multiplexer_5 (
    .in0(multiplexer_4_out), .in1(1'b1), .out(multiplexer_5_out), .sel(U_lui));
  Comparator #(.width(7), .mode("unsigned")) comparator_5 (.a(opcode), .b(7'b0010011), .eq(I_ALU));  // open: gt, lt
  Comparator #(.width(7), .mode("unsigned")) comparator_6 (.a(opcode), .b(7'b0000011), .eq(MemtoReg));  // open: gt, lt
  assign bit_extender_1_out = {{2{opcode[5]}}, opcode[5]};  // Bit_Extender bit_extender_1
  Multiplexer #(.width(3), .enable("false")) multiplexer_6 (
    .in0(multiplexer_3_out), .in1(bit_extender_1_out), .out(multiplexer_6_out), .sel(or_1_out));
  or or_1 (or_1_out, U_lui, U_auipc);
  or or_2 (or_2_out, I_jalr, ExtOp[2], MemtoReg, MemWr, B_type, U_auipc);
  Comparator #(.width(7), .mode("unsigned")) comparator_7 (.a(opcode), .b(7'b0110011), .eq(R_type));  // open: gt, lt
  Comparator #(.width(7), .mode("unsigned")) comparator_8 (.a(opcode), .b(7'b0100011), .eq(MemWr));  // open: gt, lt
  Multiplexer #(.select(3), .width(3), .disabled(0), .enable("false")) multiplexer_7 (
    .in0(3'b100), .in1(3'b101), .in4(3'b110), .in5(3'b111), .in6(3'b110), .in7(3'b111),
    .out(multiplexer_7_out), .sel(funct3));  // open: in2, in3
  Multiplexer #(.width(3), .enable("false")) multiplexer_8 (
    .in0(3'b000), .in1(multiplexer_7_out), .out(multiplexer_8_out), .sel(B_type));
  Multiplexer #(.width(3), .enable("false")) multiplexer_9 (
    .in0(multiplexer_6_out), .in1(3'b000), .out(multiplexer_9_out), .sel(or_3_out));
  or or_3 (or_3_out, MemWr, ExtOp[2], MemtoReg);
  or or_4 (or_4_out, I_ALU, R_type, I_jalr);
  Multiplexer #(.enable("false")) multiplexer_10 (.in0(multiplexer_5_out), .in1(1'b0), .out(ALUctr[3]), .sel(or_2_out));
  Multiplexer #(.select(3), .width(3), .disabled(0)) multiplexer_11 (
    .in0(3'b101), .in1(3'b110), .in2(3'b000), .in3(3'b000), .in4(3'b001), .in5(3'b010), .in6(3'b000),
    .in7(3'b000), .out(MemOp), .sel(funct3), .en(or_5_out));
  or or_5 (or_5_out, MemtoReg, MemWr);
  Multiplexer #(.width(3), .enable("false")) multiplexer_12 (
    .in0(multiplexer_8_out), .in1(3'b010), .out(multiplexer_12_out), .sel(I_jalr));
  Multiplexer #(.width(3), .enable("false")) multiplexer_13 (
    .in0(multiplexer_9_out), .in1(funct3), .out(ALUctr[2:0]), .sel(or_4_out));
  Comparator #(.width(7), .mode("unsigned")) comparator_9 (.a(opcode), .b(7'b1101111), .eq(ExtOp[2]));  // open: gt, lt
  Comparator #(.width(7), .mode("unsigned")) comparator_10 (.a(opcode), .b(7'b1110011), .eq(Halt));  // open: gt, lt
  or or_6 (RegWr, U_lui, U_auipc, I_ALU, R_type, ExtOp[2], I_jalr, MemtoReg);
  or or_7 (ALUASrc, U_auipc, ExtOp[2], I_jalr);
  or or_8 (ALUBSrc[0], ExtOp[2], I_jalr);
  or or_9 (ALUBSrc[1], U_lui, U_auipc, I_ALU, MemtoReg, MemWr);
  or or_10 (ExtOp[0], U_lui, U_auipc, B_type);
  or or_11 (ExtOp[1], B_type, MemWr);
  Multiplexer #(.width(3), .enable("false")) multiplexer_14 (
    .in0(multiplexer_12_out), .in1(3'b001), .out(multiplexer_14_out), .sel(ExtOp[2]));
  Multiplexer #(.width(3), .enable("false")) multiplexer_15 (
    .in0(3'b000), .in1(multiplexer_14_out), .out(Branch), .sel(or_12_out));
  or or_12 (or_12_out, ExtOp[2], I_jalr, B_type);

  // Other names for the same wires on the sheet: J_jal = ExtOp[2]; load = MemtoReg; store = MemWr

  // Notes on the sheet:
  //   输入引脚
  //   请勿修改引脚名称、电路名称及电路封装外观
  //   提示：根据指令种类，把7位指令code用一位指令类型标志位来表示，再通过功能码来区分具体指令，生成控制信号。
  //   输出引脚
endmodule
